# Fritzing sketch raspi-cookieclicker-cheat (saved by Fritzing 0.9.4)
breadboards: 1

parts:
  MCU1 = Raspberry Pi Zero
  Part1 = KY-019 5V Relay Module [package="Breakout board"]
  U1 = Coin [package=touch1]

nets:
  N1: MCU1.pin_2, Part1.+
  N2: MCU1.pin_6, Part1.-, Part1.Common
  N3: MCU1.pin_12, MCU1.pin_33, Part1.S
  N4: Part1.NO, U1.T1

notes:
  5cts (€) ø 21.25mm
  Copper-covered steel coin
  Rests on the screen where the touch is supposed to happen.
  5VDC Relay
  Top: GND, VCC, Signal
  Bottom: NO, COM, NC
  Raspberry Pi Zero WH
  GPIO OUT (3V3), GND, VCC (5V)

custom parts:
  KY-019 5V Relay Module: KY-019 5V Relay module, used to control AC circuits.
  Coin: Electrode for resistive touch detection
